// Logisim project CPU.circ as structural Verilog
module SFIFU (
  input  op0,
  input  op1,
  input  op2,
  input  op3,
  input  op4,
  input  op5,
  input  funct0,
  input  funct1,
  input  funct2,
  input  funct3,
  input  funct4,
  input  funct5,
  output add,
  output addi,
  output addiu,
  output addu,
  output \and ,
  output andi,
  output sll,
  output sra,
  output srl,
  output sub,
  output \or ,
  output ori
);

  wire not_1_out, not_2_out, not_3_out, not_4_out, not_5_out, not_6_out, not_7_out, not_8_out, not_9_out,
       not_10_out, not_11_out, not_12_out, not_13_out, not_14_out, not_15_out, not_16_out, not_17_out,
       not_18_out, not_19_out, not_20_out, not_21_out, not_22_out, not_23_out, not_24_out, not_25_out,
       not_26_out, not_27_out, not_28_out, not_29_out, not_30_out, not_31_out, not_32_out, not_33_out,
       not_34_out, not_35_out, not_36_out, not_37_out, not_38_out, not_39_out, not_40_out, not_41_out,
       not_42_out, not_43_out, not_44_out, not_45_out, not_46_out, not_47_out, not_48_out, not_49_out,
       not_50_out, not_51_out, not_52_out, not_53_out, not_54_out, not_55_out, not_56_out, not_57_out,
       not_58_out, not_59_out, not_60_out, not_61_out, not_62_out, not_63_out, not_64_out, not_65_out,
       not_66_out, not_67_out, not_68_out, not_69_out, not_70_out, not_71_out, not_72_out, not_73_out,
       not_74_out, not_75_out, not_76_out, not_77_out, not_78_out, not_79_out, not_80_out, not_81_out,
       not_82_out, not_83_out, not_84_out, not_85_out, not_86_out, not_87_out, not_88_out, not_89_out,
       not_90_out, not_91_out, not_92_out, not_93_out, not_94_out, not_95_out, not_96_out, not_97_out,
       not_98_out, not_99_out;

  not not_1 (not_1_out, op0);
  not not_2 (not_2_out, op1);
  not not_3 (not_3_out, op2);
  not not_4 (not_4_out, op3);
  not not_5 (not_5_out, op4);
  not not_6 (not_6_out, op5);
  not not_7 (not_7_out, funct1);
  not not_8 (not_8_out, funct2);
  not not_9 (not_9_out, funct3);
  not not_10 (not_10_out, funct4);
  not not_11 (not_11_out, funct5);
  not not_12 (not_12_out, op0);
  not not_13 (not_13_out, op1);
  not not_14 (not_14_out, op3);
  not not_15 (not_15_out, op4);
  not not_16 (not_16_out, op5);
  not not_17 (not_17_out, op0);
  not not_18 (not_18_out, op1);
  not not_19 (not_19_out, op3);
  not not_20 (not_20_out, op4);
  not not_21 (not_21_out, op0);
  not not_22 (not_22_out, op1);
  not not_23 (not_23_out, op2);
  not not_24 (not_24_out, op3);
  not not_25 (not_25_out, op4);
  not not_26 (not_26_out, op5);
  not not_27 (not_27_out, funct1);
  not not_28 (not_28_out, funct2);
  not not_29 (not_29_out, funct3);
  not not_30 (not_30_out, funct4);
  not not_31 (not_31_out, op0);
  not not_32 (not_32_out, op1);
  not not_33 (not_33_out, op2);
  not not_34 (not_34_out, op3);
  not not_35 (not_35_out, op4);
  not not_36 (not_36_out, op5);
  not not_37 (not_37_out, funct1);
  not not_38 (not_38_out, funct2);
  not not_39 (not_39_out, funct4);
  not not_40 (not_40_out, funct5);
  not not_41 (not_41_out, op0);
  not not_42 (not_42_out, op1);
  not not_43 (not_43_out, op4);
  not not_44 (not_44_out, op5);
  not not_45 (not_45_out, op0);
  not not_46 (not_46_out, op1);
  not not_47 (not_47_out, op2);
  not not_48 (not_48_out, op3);
  not not_49 (not_49_out, op4);
  not not_50 (not_50_out, op5);
  not not_51 (not_51_out, funct0);
  not not_52 (not_52_out, funct1);
  not not_53 (not_53_out, funct2);
  not not_54 (not_54_out, funct3);
  not not_55 (not_55_out, funct4);
  not not_56 (not_56_out, funct5);
  not not_57 (not_57_out, op0);
  not not_58 (not_58_out, op1);
  not not_59 (not_59_out, op2);
  not not_60 (not_60_out, op3);
  not not_61 (not_61_out, op4);
  not not_62 (not_62_out, op5);
  not not_63 (not_63_out, funct0);
  not not_64 (not_64_out, funct1);
  not not_65 (not_65_out, funct2);
  not not_66 (not_66_out, funct3);
  not not_67 (not_67_out, op0);
  not not_68 (not_68_out, op1);
  not not_69 (not_69_out, op2);
  not not_70 (not_70_out, op3);
  not not_71 (not_71_out, op4);
  not not_72 (not_72_out, op5);
  not not_73 (not_73_out, funct0);
  not not_74 (not_74_out, funct1);
  not not_75 (not_75_out, funct2);
  not not_76 (not_76_out, funct3);
  not not_77 (not_77_out, funct5);
  not not_78 (not_78_out, op0);
  not not_79 (not_79_out, op1);
  not not_80 (not_80_out, op2);
  not not_81 (not_81_out, op3);
  not not_82 (not_82_out, op4);
  not not_83 (not_83_out, op5);
  not not_84 (not_84_out, funct1);
  not not_85 (not_85_out, funct2);
  not not_86 (not_86_out, funct3);
  not not_87 (not_87_out, funct5);
  not not_88 (not_88_out, op0);
  not not_89 (not_89_out, op1);
  not not_90 (not_90_out, op2);
  not not_91 (not_91_out, op3);
  not not_92 (not_92_out, op4);
  not not_93 (not_93_out, op5);
  not not_94 (not_94_out, funct1);
  not not_95 (not_95_out, funct2);
  not not_96 (not_96_out, funct4);
  not not_97 (not_97_out, op0);
  not not_98 (not_98_out, op1);
  not not_99 (not_99_out, op4);
  and and_1 (add, not_1_out, not_2_out, not_3_out, not_4_out, not_5_out, not_6_out, funct0, not_7_out, not_8_out, not_9_out, not_10_out, not_11_out);
  and and_2 (addi, not_12_out, not_13_out, op2, not_14_out, not_15_out, not_16_out);
  and and_3 (addiu, not_17_out, not_18_out, op2, not_19_out, not_20_out, op5);
  and and_4 (addu, not_21_out, not_22_out, not_23_out, not_24_out, not_25_out, not_26_out, funct0, not_27_out, not_28_out, not_29_out, not_30_out, funct5);
  and and_5 (\and , not_31_out, not_32_out, not_33_out, not_34_out, not_35_out, not_36_out, funct0, not_37_out, not_38_out, funct3, not_39_out, not_40_out);
  and and_6 (andi, not_41_out, not_42_out, op2, op3, not_43_out, not_44_out);
  and and_7 (sll, not_45_out, not_46_out, not_47_out, not_48_out, not_49_out, not_50_out, not_51_out, not_52_out, not_53_out, not_54_out, not_55_out, not_56_out);
  and and_8 (sra, not_57_out, not_58_out, not_59_out, not_60_out, not_61_out, not_62_out, not_63_out, not_64_out, not_65_out, not_66_out, funct4, funct5);
  and and_9 (srl, not_67_out, not_68_out, not_69_out, not_70_out, not_71_out, not_72_out, not_73_out, not_74_out, not_75_out, not_76_out, funct4, not_77_out);
  and and_10 (sub, not_78_out, not_79_out, not_80_out, not_81_out, not_82_out, not_83_out, funct0, not_84_out, not_85_out, not_86_out, funct4, not_87_out);
  and and_11 (\or , not_88_out, not_89_out, not_90_out, not_91_out, not_92_out, not_93_out, funct0, not_94_out, not_95_out, funct3, not_96_out, funct5);
  and and_12 (ori, not_97_out, not_98_out, op2, op3, not_99_out, op5);
endmodule

module STIFU (
  input  op0,
  input  op1,
  input  op2,
  input  op3,
  input  op4,
  input  op5,
  input  funct0,
  input  funct1,
  input  funct2,
  input  funct3,
  input  funct4,
  input  funct5,
  output \nor ,
  output lw,
  output sw,
  output beq,
  output bne,
  output slt,
  output slti,
  output sltu,
  output j,
  output jal,
  output jr,
  output syscall
);

  wire not_1_out, not_2_out, not_3_out, not_4_out, not_5_out, not_6_out, not_7_out, not_8_out, not_9_out,
       not_10_out, not_11_out, not_12_out, not_13_out, not_14_out, not_15_out, not_16_out, not_17_out,
       not_18_out, not_19_out, not_20_out, not_21_out, not_22_out, not_23_out, not_24_out, not_25_out,
       not_26_out, not_27_out, not_28_out, not_29_out, not_30_out, not_31_out, not_32_out, not_33_out,
       not_34_out, not_35_out, not_36_out, not_37_out, not_38_out, not_39_out, not_40_out, not_41_out,
       not_42_out, not_43_out, not_44_out, not_45_out, not_46_out, not_47_out, not_48_out, not_49_out,
       not_50_out, not_51_out, not_52_out, not_53_out, not_54_out, not_55_out, not_56_out, not_57_out,
       not_58_out, not_59_out, not_60_out, not_61_out, not_62_out, not_63_out, not_64_out, not_65_out,
       not_66_out, not_67_out, not_68_out, not_69_out, not_70_out, not_71_out, not_72_out, not_73_out;

  not not_1 (not_1_out, op0);
  not not_2 (not_2_out, op1);
  not not_3 (not_3_out, op2);
  not not_4 (not_4_out, op3);
  not not_5 (not_5_out, op4);
  not not_6 (not_6_out, op5);
  not not_7 (not_7_out, funct1);
  not not_8 (not_8_out, funct2);
  not not_9 (not_9_out, op1);
  not not_10 (not_10_out, op2);
  not not_11 (not_11_out, op3);
  not not_12 (not_12_out, op1);
  not not_13 (not_13_out, op3);
  not not_14 (not_14_out, op0);
  not not_15 (not_15_out, op1);
  not not_16 (not_16_out, op2);
  not not_17 (not_17_out, op4);
  not not_18 (not_18_out, op5);
  not not_19 (not_19_out, op0);
  not not_20 (not_20_out, op1);
  not not_21 (not_21_out, op2);
  not not_22 (not_22_out, op4);
  not not_23 (not_23_out, op0);
  not not_24 (not_24_out, op1);
  not not_25 (not_25_out, op2);
  not not_26 (not_26_out, op3);
  not not_27 (not_27_out, op4);
  not not_28 (not_28_out, op5);
  not not_29 (not_29_out, funct1);
  not not_30 (not_30_out, funct3);
  not not_31 (not_31_out, funct5);
  not not_32 (not_32_out, op0);
  not not_33 (not_33_out, op1);
  not not_34 (not_34_out, op3);
  not not_35 (not_35_out, op5);
  not not_36 (not_36_out, op0);
  not not_37 (not_37_out, op1);
  not not_38 (not_38_out, op2);
  not not_39 (not_39_out, op3);
  not not_40 (not_40_out, op4);
  not not_41 (not_41_out, op5);
  not not_42 (not_42_out, funct1);
  not not_43 (not_43_out, funct3);
  not not_44 (not_44_out, op0);
  not not_45 (not_45_out, op1);
  not not_46 (not_46_out, op2);
  not not_47 (not_47_out, op3);
  not not_48 (not_48_out, op5);
  not not_49 (not_49_out, op0);
  not not_50 (not_50_out, op1);
  not not_51 (not_51_out, op2);
  not not_52 (not_52_out, op3);
  not not_53 (not_53_out, op0);
  not not_54 (not_54_out, op1);
  not not_55 (not_55_out, op2);
  not not_56 (not_56_out, op3);
  not not_57 (not_57_out, op4);
  not not_58 (not_58_out, op5);
  not not_59 (not_59_out, funct0);
  not not_60 (not_60_out, funct1);
  not not_61 (not_61_out, funct3);
  not not_62 (not_62_out, funct4);
  not not_63 (not_63_out, funct5);
  not not_64 (not_64_out, op0);
  not not_65 (not_65_out, op1);
  not not_66 (not_66_out, op2);
  not not_67 (not_67_out, op3);
  not not_68 (not_68_out, op4);
  not not_69 (not_69_out, op5);
  not not_70 (not_70_out, funct0);
  not not_71 (not_71_out, funct1);
  not not_72 (not_72_out, funct4);
  not not_73 (not_73_out, funct5);
  and and_1 (\nor , not_1_out, not_2_out, not_3_out, not_4_out, not_5_out, not_6_out, funct0, not_7_out, not_8_out, funct3, funct4, funct5);
  and and_2 (lw, op0, not_9_out, not_10_out, not_11_out, op4, op5);
  and and_3 (sw, op0, not_12_out, op2, not_13_out, op4, op5);
  and and_4 (beq, not_14_out, not_15_out, not_16_out, op3, not_17_out, not_18_out);
  and and_5 (bne, not_19_out, not_20_out, not_21_out, op3, not_22_out, op5);
  and and_6 (slt, not_23_out, not_24_out, not_25_out, not_26_out, not_27_out, not_28_out, funct0, not_29_out, funct2, not_30_out, funct4, not_31_out);
  and and_7 (slti, not_32_out, not_33_out, op2, not_34_out, op4, not_35_out);
  and and_8 (sltu, not_36_out, not_37_out, not_38_out, not_39_out, not_40_out, not_41_out, funct0, not_42_out, funct2, not_43_out, funct4, funct5);
  and and_9 (j, not_44_out, not_45_out, not_46_out, not_47_out, op4, not_48_out);
  and and_10 (jal, not_49_out, not_50_out, not_51_out, not_52_out, op4, op5);
  and and_11 (jr, not_53_out, not_54_out, not_55_out, not_56_out, not_57_out, not_58_out, not_59_out, not_60_out, funct2, not_61_out, not_62_out, not_63_out);
  and and_12 (syscall, not_64_out, not_65_out, not_66_out, not_67_out, not_68_out, not_69_out, not_70_out, not_71_out, funct2, funct3, not_72_out, not_73_out);
endmodule
