// Logisim project alu.circ as structural Verilog: 4 circuits, main circuit ALU
module ALU (
  input  [31:0] X,
  input  [31:0] Y,
  input  [3:0] AluOP,
  output Signed_Overflow,
  output UnSigned_Overflow,
  output Equal,
  output [31:0] Result,
  output [31:0] Result_2
);

  wire [31:0] Result2;

  // Probe on X
  // Probe on X
  // Probe on Y
  // Probe on Y
  // Probe on AluOP
  // Probe on Result
  // Probe on Result
  // Probe on Result2

  // Other names for the same wires on the sheet: OF = Signed_Overflow; S[3:0] = AluOP; UOF = UnSigned_Overflow

  // Notes on the sheet:
  //   不要改变此引脚区域内容，也不要改变ALU封装形式
  //   输入引脚
  //   请在下方利用上方输入输出引脚的隧道信号构建ALU电路，ctrl+d复制选择部件
  //   华中科技大学计算机学院 计算机组成原理，鸣谢加州大学伯克利CS61C课程
  //   输出引脚
  //   探测区域
endmodule

module \演示电路  (
  input  [31:0] X,
  input  [31:0] Y,
  input  [3:0] ALUOP,
  output Signed_Overflow,
  output Unsigned_overflow,
  output [31:0] Result,
  output [31:0] Result_2,
  output Equal
);

  // Probe on X
  // Probe on X
  ALU alu_1 (
    .AluOP(ALUOP), .X(X), .Equal(Equal), .Result(Result), .Signed_Overflow(Signed_Overflow), .Y(Y),
    .Result_2(Result_2), .UnSigned_Overflow(Unsigned_overflow));
  // Probe on ALUOP
  // Probe on Y
  // Probe on Y
  // Probe on Result
  // Probe on Result
  // Probe on Result_2

  // Notes on the sheet:
  //   ALu电路无需调整位置即可连接在该电路中，并且不能出现蓝色线缆和三态输出
endmodule

module \等差数列  (
  input  [31:0] \数列初始值 ,
  input  [31:0] \等差值 ,
  input  \时钟 ,
  output [31:0] Result
);

  // Probe on \数列初始值 
  // Probe on \数列初始值 
  // Probe on \等差值 
  // Probe on \等差值 
  // Probe on Result
  // Probe on Result

  // Other names for the same wires on the sheet: 数列初值[31:0] = \数列初始值 ; 累加和[31:0] = Result

  // Notes on the sheet:
  //   不要改变此引脚区域内容，也不要改变ALU封装形式
  //   请在下方利用上方输入输出引脚的隧道信号构建等差数列求和电路，ctrl+d复制选择部件
  //   华中科技大学计算机学院 计算机组成原理，鸣谢加州大学伯克利CS61C课程
  //   输出引脚
  //   探测区域
endmodule

module PARADD (
  input  [3:0] in_1,
  input  [3:0] in_2,
  input  C0
);

  wire and_1_out, and_2_out, and_3_out, and_4_out, and_5_out, and_6_out, and_7_out, and_8_out, and_9_out,
       and_10_out, C1_out, C2_out, C3_out, C4_out;
  wire [3:0] PRO_out, TRAN_out;

  and and_1 (and_1_out, PRO_out[2], TRAN_out[3]);
  // Probe on C4_out
  ExactlyOne C4 (.out(C4_out), .in0(PRO_out[3]), .in1(and_1_out), .in2(and_2_out), .in3(and_3_out), .in4(and_4_out));
  and and_2 (and_2_out, PRO_out[1], TRAN_out[3], TRAN_out[2]);
  and and_3 (and_3_out, PRO_out[0], TRAN_out[3], TRAN_out[2], TRAN_out[1]);
  and and_4 (and_4_out, TRAN_out[3], TRAN_out[2], TRAN_out[1], TRAN_out[0], C0);
  // Probe on C3_out
  ExactlyOne C3 (.out(C3_out), .in0(PRO_out[2]), .in1(and_5_out), .in2(and_6_out), .in3(and_7_out));
  and and_5 (and_5_out, PRO_out[1], TRAN_out[2]);
  assign PRO_out = in_1 & in_2;  // AND_Gate PRO, 4 bits wide
  and and_6 (and_6_out, PRO_out[0], TRAN_out[1]);
  and and_7 (and_7_out, TRAN_out[2], TRAN_out[1], TRAN_out[0], C0);
  // Probe on C2_out
  ExactlyOne C2 (.out(C2_out), .in0(PRO_out[1]), .in1(and_8_out), .in2(and_9_out));
  and and_8 (and_8_out, PRO_out[0], TRAN_out[1]);
  and and_9 (and_9_out, TRAN_out[1], TRAN_out[0], C0);
  assign TRAN_out = in_1 ^ in_2;  // XOR_Gate TRAN, 4 bits wide
  // Probe on C1_out
  xor C1 (C1_out, PRO_out[0], and_10_out);
  and and_10 (and_10_out, TRAN_out[0], C0);
endmodule
